# Fritzing sketch rees31 (saved by Fritzing 0.8.7b)
breadboards: 1

parts:
  MD09B1 = A4988 Stepper Motor Driver Carrier
  S1 = Momentary Switch [package=ksa_sealed_tac_switch]
  S2 = Momentary Switch [package=ksa_sealed_tac_switch]
  S3 = Momentary Switch [package=ksa_sealed_tac_switch]
  Power_plug1 = Power plug
  U1 = Voltage Regulator - 5V [package="TO220 [THT]"]
  Parte1 = Arduino Pro Mini v13
  Parte2 = Arduino Pro Mini v13
  M1 = Stepper Motor - Bipolar
  D2F2 = D2F-FL Omron Snap Action Limit Switch with Level

nets:
  N1: MD09B1.MS1, MD09B1.MS2, MD09B1.MS3, MD09B1.RESET, MD09B1.SLEEP, MD09B1.VDD
  N2: MD09B1.STEP, Parte1.D2
  N3: MD09B1.DIR, Parte1.D5_PWM
  N4: MD09B1.VMOT, Power_plug1.VCC, U1.input_voltage
  GND: MD09B1.GROUND, S1.1, S2.1, S3.4, Power_plug1.GND, U1.GND, Parte1.GND, D2F2.COM
  N5: MD09B1.OUT_2B, M1.A
  N6: MD09B1.OUT_2A, M1.C
  N7: MD09B1.OUT_1A, M1.B
  N8: MD09B1.OUT_1B, M1.D
  N9: S1.4, Parte2.D5_PWM
  N10: S2.4, Parte2.D3_PWM
  N11: S3.1, Parte2.D4
  N12: U1.output_voltage, Parte1.VCC
  N13: Parte1.D1/RX, Parte2.D0/TX
  N14: Parte1.D0/TX, Parte2.D1/RX
  N15: Parte2.D6_PWM, D2F2.NC

custom parts:
  D2F-FL Omron Snap Action Limit Switch with Level: Snap action switch with stainless steel lever.
